# Fritzing sketch VISSible Cells Sketch ULN2003an NodeMCU PCB (saved by Fritzing 0.9.10b)
circuit board: 8.46667cm x 5.64444cm
breadboards: 7

parts:
  U2 = Vibration Motor- ROB-08449 [package=vibe-motor-10mm]
  D2 = Diode [package=diode-1n4148]
  R2 = Resistor [tolerance=±5% resistance=1k package="0603 [SMD]"]
  R3 = Resistor [tolerance=±5% resistance=1k package="0603 [SMD]"]
  R4 = Resistor [tolerance=±5% resistance=1k package="0603 [SMD]"]
  R5 = Resistor [tolerance=±5% resistance=1k package="0603 [SMD]"]
  R6 = Resistor [tolerance=±5% resistance=1k package="0603 [SMD]"]
  R7 = Resistor [tolerance=±5% resistance=1k package="0603 [SMD]"]
  R8 = Resistor [tolerance=±5% resistance=1k package="0603 [SMD]"]
  U3 = Vibration Motor- ROB-08449 [package=vibe-motor-10mm]
  D3 = Diode [package=diode-1n4148]
  U4 = Vibration Motor- ROB-08449 [package=vibe-motor-10mm]
  D4 = Diode [package=diode-1n4148]
  U5 = Vibration Motor- ROB-08449 [package=vibe-motor-10mm]
  D5 = Diode [package=diode-1n4148]
  U6 = Vibration Motor- ROB-08449 [package=vibe-motor-10mm]
  D6 = Diode [package=diode-1n4148]
  U7 = Vibration Motor- ROB-08449 [package=vibe-motor-10mm]
  D7 = Diode [package=diode-1n4148]
  Mod1 = Amica NodeMCU DEVKIT 1.0
  U8 = 74HC595 [package="DIP16 [THT]"]
  IC2 = ULN2003A [package="DIP16 [THT]"]
  J2 = female pin header, 6 pins [form="♀ (female)"]

nets:
  N1: U2.+, IC2.Out_1
  N2: U2.-, D2.C, Mod1.pin_10, U8.VCC, J2.pin1
  N3: R2.Pin_0, R2.Pin_1, U8.Q7, IC2.In_1
  N4: R3.Pin_0, R3.Pin_1, U8.Q6, IC2.In_2
  N5: R4.Pin_0, R4.Pin_1, U8.Q5, IC2.In_3
  N6: R5.Pin_0, R5.Pin_1, U8.Q4, IC2.In_4
  N7: R6.Pin_0, R6.Pin_1, U8.Q3, IC2.In_5
  N8: R7.Pin_0, R7.Pin_1, U8.Q2, IC2.In_6
  N9: R8.Pin_0, R8.Pin_1, U8.Q1, IC2.In_7
  N10: U3.+, IC2.Out_2
  N11: U3.-, D3.C, U4.-, D4.C, U5.-, D5.C, U6.-, D6.C, U7.-, D7.C, Mod1.pin_9, U8.GND, U8.OE, IC2.0V, J2.pin3
  N12: U4.+, IC2.Out_3
  N13: U5.+, IC2.Out_4
  N14: U6.+, IC2.Out_5
  N15: U7.+, IC2.Out_6
  N16: Mod1.pin_11, U8.DS, J2.pin2
  N17: Mod1.pin_12, U8.ST_CP, J2.pin4
  N18: Mod1.pin_13, U8.SH_CP, J2.pin5
  N19: Mod1.pin_14, U8.MR, J2.pin6
